// Logisim project Circuitos completo.circ as structural Verilog: 23 circuits, main circuit main
module main (
  input  Reset,
  output [7:0] out_2,
  output [4:0] out_3
);

  wire CLK, Cmem, Cpc, CpuClock_out, Ealu, Ear, Eir, Epc, HLT, Lar, Lbr, Lir, Lmar, Lor, nCLK, nCLR,
       not_1_out, not_4_out, not_5_out, or_1_out, Regist_de_Instr_i5, Regist_de_Instr_i6, Regist_de_Instr_i7,
       Salu;
  wire [6:0] bit_extender_1_out;
  wire [7:0] acumulador_1_out_ula, contador_de_programa_1_out, Registrador_B_out_ula;

  Clock CpuClock (.out(CpuClock_out));
  not not_1 (not_1_out, HLT);
  and and_1 (CLK, not_1_out, CpuClock_out);
  not not_2 (nCLK, CLK);
  not not_3 (nCLR, Reset);
  or or_1 (or_1_out, CLK, Reset);
  \Registrador_de_Endereços  \registrador_de_endereços_1  (
    .In(contador_de_programa_1_out), .Lmar(Lmar), .Clk(CLK), .Clr(Reset), .Out(out_3));
  not not_4 (not_4_out, Cmem);
  Controlador_Sequenciador controlador_sequenciador_1 (
    .Clk(or_1_out), .Reset(Reset), .I7(Regist_de_Instr_i7), .I6(Regist_de_Instr_i6), .I5(Regist_de_Instr_i5),
    .Cpc(Cpc), .Cmem(Cmem), .Salu(Salu), .Lir(Lir), .Lor(Lor), .Lbr(Lbr), .HLT(HLT), .Lar(Lar), .Lmar(Lmar),
    .Ear(Ear), .Ealu(Ealu), .Eir(Eir), .Epc(Epc));
  Contador_de_Programa contador_de_programa_1 (
    .Cpc(Cpc), .CLK(nCLK), .CLR(Reset), .Epc(Epc), .Out(contador_de_programa_1_out));
  Registrador_IR Regist_de_Instr (
    .In(contador_de_programa_1_out), .Lir(Lir), .Clk(CLK), .Clr(Reset), .Eir(Eir),
    .Out(contador_de_programa_1_out), .I5(Regist_de_Instr_i5), .I6(Regist_de_Instr_i6),
    .I7(Regist_de_Instr_i7));
  RAM #(.addrWidth(5)) ram_1 (
    .addr(out_3), .data(contador_de_programa_1_out), .sel(not_4_out), .clk(CLK), .ld(not_4_out));  // open: clr
  Acumulador acumulador_1 (
    .In(contador_de_programa_1_out), .Lar(Lar), .Clk(CLK), .Clr(Reset), .Ear(Ear),
    .Out_ULA(acumulador_1_out_ula), .Out(contador_de_programa_1_out));
  Somador_Subtrator somador_subtrator_1 (
    .A(acumulador_1_out_ula), .B(Registrador_B_out_ula), .Salu(Salu), .Out(contador_de_programa_1_out),
    .Ealu(Ealu));
  Registrador_B Registrador_B (
    .In(contador_de_programa_1_out), .Lbr(Lbr), .Clk(CLK), .Clr(Reset), .Out_ULA(Registrador_B_out_ula));
  Bit_Extender #(.out_width(7)) bit_extender_1 (.in(contador_de_programa_1_out), .out(bit_extender_1_out));
  TTY tty_1 (.data(bit_extender_1_out), .clk(CLK), .we(not_5_out), .clr(Reset));
  not not_5 (not_5_out, Lor);

  // Other names for the same wires on the sheet: CLR = Reset
endmodule

module Latch_RS (
  input  Clr,
  input  R,
  input  E,
  input  S,
  input  Pre,
  output Q,
  output out_7
);

  wire and_1_out, and_2_out, or_1_out, or_2_out;

  and and_1 (and_1_out, R, E);
  and and_2 (and_2_out, E, S);
  or or_1 (or_1_out, Clr, and_1_out);
  or or_2 (or_2_out, and_2_out, Pre);
  nor nor_1 (Q, or_1_out, out_7);
  nor nor_2 (out_7, Q, or_2_out);
endmodule

// FF RS
module Flip_Flop_RS (
  input  R,
  input  S,
  input  Clk,
  input  Pre,
  input  Clr,
  output Q,
  output nQ
);

  wire latch_rs_1_out_7, latch_rs_1_q, not_1_out;

  not not_1 (not_1_out, Clk);
  Latch_RS latch_rs_1 (.Clr(Clr), .R(R), .E(not_1_out), .S(S), .Pre(Pre), .Q(latch_rs_1_q), .out_7(latch_rs_1_out_7));
  Latch_RS latch_rs_2 (.Clr(Clr), .R(latch_rs_1_out_7), .E(Clk), .S(latch_rs_1_q), .Pre(Pre), .Q(Q), .out_7(nQ));
endmodule

module MUX2 (
  input  A,
  input  B,
  input  SEL,
  output Y
);

  wire and_1_out, and_2_out, not_1_out;

  not not_1 (not_1_out, SEL);
  and and_1 (and_1_out, A, not_1_out);
  and and_2 (and_2_out, B, SEL);
  or or_1 (Y, and_1_out, and_2_out);
endmodule

module MUX2x8 (
  input  [7:0] A,
  input  [7:0] B,
  input  SEL,
  output [7:0] out_4
);

  MUX2 mux2_1 (.A(A[0]), .Y(out_4[0]), .B(B[0]), .SEL(SEL));
  MUX2 mux2_2 (.A(A[1]), .Y(out_4[1]), .B(B[1]), .SEL(SEL));
  MUX2 mux2_3 (.A(A[2]), .Y(out_4[2]), .B(B[2]), .SEL(SEL));
  MUX2 mux2_4 (.A(A[3]), .Y(out_4[3]), .B(B[3]), .SEL(SEL));
  MUX2 mux2_5 (.A(A[4]), .Y(out_4[4]), .B(B[4]), .SEL(SEL));
  MUX2 mux2_6 (.A(A[5]), .Y(out_4[5]), .B(B[5]), .SEL(SEL));
  MUX2 mux2_7 (.A(A[6]), .Y(out_4[6]), .B(B[6]), .SEL(SEL));
  MUX2 mux2_8 (.A(A[7]), .Y(out_4[7]), .B(B[7]), .SEL(SEL));
endmodule

module Somador_Completo (
  input  A,
  input  B,
  input  Ci,
  output R,
  output Co
);

  wire and_1_out, and_2_out, xor_1_out;

  xor xor_1 (xor_1_out, A, B);
  xor xor_2 (R, xor_1_out, Ci);
  and and_1 (and_1_out, A, B);
  and and_2 (and_2_out, xor_1_out, Ci);
  or or_1 (Co, and_1_out, and_2_out);
endmodule

module Somador_8_bits (
  input  Ci,
  input  [7:0] A,
  input  [7:0] B,
  output [7:0] R
);

  wire somador_completo_1_co, somador_completo_2_co, somador_completo_3_co, somador_completo_4_co,
       somador_completo_5_co, somador_completo_6_co, somador_completo_7_co;

  Somador_Completo somador_completo_1 (.A(A[0]), .B(B[0]), .Ci(Ci), .R(R[0]), .Co(somador_completo_1_co));
  Somador_Completo somador_completo_2 (
    .A(A[1]), .B(B[1]), .Ci(somador_completo_1_co), .R(R[1]), .Co(somador_completo_2_co));
  Somador_Completo somador_completo_3 (
    .A(A[2]), .B(B[2]), .Ci(somador_completo_2_co), .R(R[2]), .Co(somador_completo_3_co));
  Somador_Completo somador_completo_4 (
    .A(A[3]), .B(B[3]), .Ci(somador_completo_3_co), .R(R[3]), .Co(somador_completo_4_co));
  Somador_Completo somador_completo_5 (
    .A(A[4]), .B(B[4]), .Ci(somador_completo_4_co), .R(R[4]), .Co(somador_completo_5_co));
  Somador_Completo somador_completo_6 (
    .A(A[5]), .B(B[5]), .Ci(somador_completo_5_co), .R(R[5]), .Co(somador_completo_6_co));
  Somador_Completo somador_completo_7 (
    .A(A[6]), .B(B[6]), .Ci(somador_completo_6_co), .R(R[6]), .Co(somador_completo_7_co));
  Somador_Completo somador_completo_8 (.A(A[7]), .B(B[7]), .Ci(somador_completo_7_co), .R(R[7]));  // open: Co
endmodule

module Flip_Flop_D (
  input  D,
  input  Clk,
  input  Pre,
  input  Clr,
  output Q
);

  wire not_1_out;

  not not_1 (not_1_out, D);
  Flip_Flop_RS Flipflop_RS (.R(not_1_out), .S(D), .Clk(Clk), .Pre(Pre), .Clr(Clr), .Q(Q));  // open: nQ
endmodule

module registrador_de_um_bit (
  input  D,
  input  Enable,
  input  Clk,
  input  Clr,
  output Q
);

  wire mux2_1_y;

  MUX2 mux2_1 (.A(Q), .Y(mux2_1_y), .B(D), .SEL(Enable));
  Flip_Flop_D Flip_Flop_D (.D(mux2_1_y), .Clk(Clk), .Pre(1'b0), .Clr(Clr), .Q(Q));
endmodule

module Registrador_de_8_bit (
  input  [7:0] D,
  input  Enable,
  input  Clk,
  input  Clr,
  output [7:0] Q
);

  wire [7:0] mux2x8_1_out_4;

  MUX2x8 mux2x8_1 (.A(Q), .B(D), .SEL(Enable), .out_4(mux2x8_1_out_4));
  Flip_Flop_D_x8 ff_d_x8_1 (.D(mux2x8_1_out_4), .Clk(Clk), .Pre(1'b0), .Clr(Clr), .Q(Q));
endmodule

module Flip_Flop_D_x8 (
  input  [7:0] D,
  input  Clk,
  input  Pre,
  input  Clr,
  output [7:0] Q
);

  wire not_1_out, not_2_out, not_3_out, not_4_out, not_5_out, not_6_out, not_7_out, not_8_out;

  not not_1 (not_1_out, D[0]);
  not not_2 (not_2_out, D[1]);
  not not_3 (not_3_out, D[2]);
  not not_4 (not_4_out, D[3]);
  not not_5 (not_5_out, D[4]);
  not not_6 (not_6_out, D[5]);
  not not_7 (not_7_out, D[6]);
  not not_8 (not_8_out, D[7]);
  Flip_Flop_RS Flipflop_RS (.R(not_1_out), .S(D[0]), .Clk(Clk), .Pre(Pre), .Clr(Clr), .Q(Q[0]));  // open: nQ
  Flip_Flop_RS Flipflop_RS_2 (.R(not_2_out), .S(D[1]), .Clk(Clk), .Pre(Pre), .Clr(Clr), .Q(Q[1]));  // open: nQ
  Flip_Flop_RS Flipflop_RS_3 (.R(not_3_out), .S(D[2]), .Clk(Clk), .Pre(Pre), .Clr(Clr), .Q(Q[2]));  // open: nQ
  Flip_Flop_RS Flipflop_RS_4 (.R(not_4_out), .S(D[3]), .Clk(Clk), .Pre(Pre), .Clr(Clr), .Q(Q[3]));  // open: nQ
  Flip_Flop_RS Flipflop_RS_5 (.R(not_5_out), .S(D[4]), .Clk(Clk), .Pre(Pre), .Clr(Clr), .Q(Q[4]));  // open: nQ
  Flip_Flop_RS Flipflop_RS_6 (.R(not_6_out), .S(D[5]), .Clk(Clk), .Pre(Pre), .Clr(Clr), .Q(Q[5]));  // open: nQ
  Flip_Flop_RS Flipflop_RS_7 (.R(not_7_out), .S(D[6]), .Clk(Clk), .Pre(Pre), .Clr(Clr), .Q(Q[6]));  // open: nQ
  Flip_Flop_RS Flipflop_RS_8 (.R(not_8_out), .S(D[7]), .Clk(Clk), .Pre(Pre), .Clr(Clr), .Q(Q[7]));  // open: nQ
endmodule

// Acumul.
module Acumulador (
  input  [7:0] In,
  input  Lar,
  input  Clk,
  input  Clr,
  input  Ear,
  output [7:0] Out_ULA,
  output [7:0] Out
);

  wire not_1_out;

  not not_1 (not_1_out, Lar);
  assign Out = Ear ? Out_ULA : 8'bz;  // Controlled_Buffer W
  Registrador_de_8_bit registrador_de_8_bit_1 (.D(In), .Enable(not_1_out), .Clk(Clk), .Clr(Clr), .Q(Out_ULA));
endmodule

module Registrador_B (
  input  [7:0] In,
  input  Lbr,
  input  Clk,
  input  Clr,
  output [7:0] Out_ULA
);

  wire not_1_out;

  not not_1 (not_1_out, Lbr);
  Registrador_de_8_bit registrador_de_8_bit_1 (.D(In), .Enable(not_1_out), .Clk(Clk), .Clr(Clr), .Q(Out_ULA));
endmodule

// Registr de End.
module \Registrador_de_Endereços  (
  input  [7:0] In,
  input  Lmar,
  input  Clk,
  input  Clr,
  output [4:0] Out
);

  wire not_1_out;
  wire [7:0] registrador_de_8_bit_1_q;

  not not_1 (not_1_out, Lmar);
  Bit_Extender #(.out_width(5)) bit_extender_1 (.in(registrador_de_8_bit_1_q), .out(Out));
  Registrador_de_8_bit registrador_de_8_bit_1 (
    .D(In), .Enable(not_1_out), .Clk(Clk), .Clr(Clr), .Q(registrador_de_8_bit_1_q));
endmodule

module Registrador_IR (
  input  [7:0] In,
  input  Lir,
  input  Clk,
  input  Clr,
  input  Eir,
  output [7:0] Out,
  output I5,
  output I6,
  output I7
);

  wire not_1_out, not_2_out;
  wire [4:0] registrador_de_8_bit_1_q;
  wire [7:0] bit_extender_1_out;

  not not_1 (not_1_out, Lir);
  not not_2 (not_2_out, Eir);
  Registrador_de_8_bit registrador_de_8_bit_1 (
    .D(In), .Enable(not_1_out), .Clk(Clk), .Clr(Clr), .Q({I7, I6, I5, registrador_de_8_bit_1_q}));
  assign bit_extender_1_out = {{3{1'b0}}, registrador_de_8_bit_1_q};  // Bit_Extender bit_extender_1
  assign Out = not_2_out ? bit_extender_1_out : 8'bz;  // Controlled_Buffer controlled_buffer_1
endmodule

module Contador_Anel (
  input  Clk,
  input  Reset,
  output T0,
  output T1,
  output T2,
  output T3,
  output T4,
  output T5
);

  Flip_Flop_D FF_D (.D(T5), .Clk(Clk), .Pre(Reset), .Clr(1'b0), .Q(T0));
  Flip_Flop_D FF_D_2 (.D(T0), .Clk(Clk), .Pre(1'b0), .Clr(Reset), .Q(T1));
  Flip_Flop_D FF_D_3 (.D(T1), .Clk(Clk), .Pre(1'b0), .Clr(Reset), .Q(T2));
  Flip_Flop_D FF_D_4 (.D(T2), .Clk(Clk), .Pre(1'b0), .Clr(Reset), .Q(T3));
  Flip_Flop_D FF_D_5 (.D(T3), .Clk(Clk), .Pre(1'b0), .Clr(Reset), .Q(T4));
  Flip_Flop_D FF_D_6 (.D(T4), .Clk(Clk), .Pre(1'b0), .Clr(Reset), .Q(T5));
endmodule

module Decoder (
  input  I7,
  input  I6,
  input  I5,
  output LDA,
  output ADD,
  output SUB,
  output OUT,
  output HLT
);

  wire not_1_out, not_2_out, not_3_out;

  not not_1 (not_1_out, I7);
  not not_2 (not_2_out, I6);
  not not_3 (not_3_out, I5);
  and and_1 (LDA, not_1_out, not_2_out, not_3_out);
  and and_2 (ADD, not_1_out, not_2_out, I5);
  and and_3 (SUB, not_1_out, I6, not_3_out);
  and and_4 (OUT, I7, I6, not_3_out);
  and and_5 (HLT, I7, I6, I5);
endmodule

module Controlador_Sequenciador (
  input  Clk,
  input  Reset,
  input  I7,
  input  I6,
  input  I5,
  output Cpc,
  output Cmem,
  output Salu,
  output Lir,
  output Lor,
  output Lbr,
  output HLT,
  output Lar,
  output Lmar,
  output Ear,
  output Ealu,
  output Eir,
  output Epc
);

  wire Contador_de_Anel_t0, Contador_de_Anel_t1, Contador_de_Anel_t2, Contador_de_Anel_t3,
       Contador_de_Anel_t4, Contador_de_Anel_t5, Decodificador_add, Decodificador_lda, Decodificador_out,
       Decodificador_sub;

  Contador_Anel Contador_de_Anel (
    .Clk(Clk), .Reset(Reset), .T0(Contador_de_Anel_t0), .T1(Contador_de_Anel_t1), .T2(Contador_de_Anel_t2),
    .T3(Contador_de_Anel_t3), .T4(Contador_de_Anel_t4), .T5(Contador_de_Anel_t5));
  Decoder Decodificador (
    .I7(I7), .I6(I6), .I5(I5), .LDA(Decodificador_lda), .ADD(Decodificador_add), .SUB(Decodificador_sub),
    .OUT(Decodificador_out), .HLT(HLT));
  Matriz_de_Controle Sinais_de_Controle (
    .T0(Contador_de_Anel_t0), .T1(Contador_de_Anel_t1), .T2(Contador_de_Anel_t2), .T3(Contador_de_Anel_t3),
    .T4(Contador_de_Anel_t4), .T5(Contador_de_Anel_t5), .LDA(Decodificador_lda), .AD(Decodificador_add),
    .SUB(Decodificador_sub), .OUT(Decodificador_out), .Cpc(Cpc), .Cmem(Cmem), .Salu(Salu), .Lir(Lir),
    .Lor(Lor), .Lbr(Lbr), .Lar(Lar), .Lmar(Lmar), .Ear(Ear), .Ealu(Ealu), .Eir(Eir), .Epc(Epc));
endmodule

module Matriz_de_Controle (
  input  T0,
  input  T1,
  input  T2,
  input  T3,
  input  T4,
  input  T5,
  input  LDA,
  input  AD,
  input  SUB,
  input  OUT,
  output Cpc,
  output Cmem,
  output Salu,
  output Lir,
  output Lor,
  output Lbr,
  output Lar,
  output Lmar,
  output Ear,
  output Ealu,
  output Eir,
  output Epc
);

  wire ADD_T3_2_out, ADD_T3_out, ADD_T4_2_out, ADD_T4_out, ADD_T5_2_out, ADD_T5_out, Cmem_out, Lbr_out,
       LDA_T3_2_out, LDA_T3_out, LDA_T4_out, Lmar_out, Lor_out, or_1_out, OUT_T3_out, SUB_T3_2_out,
       SUB_T3_out, SUB_T4_2_out, SUB_T4_out, SUB_T5_2_out, SUB_T5_3_out, T2_LDA_out;

  and T2_LDA (T2_LDA_out, LDA, T4);
  and ADD_T4 (ADD_T4_out, T4, AD);
  and SUB_T4 (SUB_T4_out, T4, SUB);
  and SUB_T5 (Salu, SUB, T5);
  and OUT_T3 (OUT_T3_out, OUT, T3);
  and ADD_T4_2 (ADD_T4_2_out, AD, T4);
  and SUB_T4_2 (SUB_T4_2_out, T4, SUB);
  and LDA_T4 (LDA_T4_out, LDA, T4);
  and ADD_T5 (ADD_T5_out, AD, T5);
  and SUB_T5_2 (SUB_T5_2_out, SUB, T5);
  and LDA_T3 (LDA_T3_out, LDA, T3);
  and ADD_T3 (ADD_T3_out, T3, AD);
  and SUB_T3 (SUB_T3_out, T3, SUB);
  and OUT_T3_2 (Ear, T3, OUT);
  and ADD_T5_2 (ADD_T5_2_out, AD, T5);
  and SUB_T5_3 (SUB_T5_3_out, SUB, T5);
  and ADD_T3_2 (ADD_T3_2_out, AD, T3);
  and LDA_T3_2 (LDA_T3_2_out, T3, LDA);
  and SUB_T3_2 (SUB_T3_2_out, T3, SUB);
  or u_Cmem (Cmem_out, T2, T2_LDA_out, ADD_T4_out, SUB_T4_out);
  or u_Lbr (Lbr_out, ADD_T4_2_out, SUB_T4_2_out);
  or u_Lor (Lor_out, LDA_T4_out, ADD_T5_out, SUB_T5_2_out);
  or u_Lmar (Lmar_out, T0, LDA_T3_out, ADD_T3_out, SUB_T3_out);
  or u_Ealu (Ealu, ADD_T5_2_out, SUB_T5_3_out);
  or or_1 (or_1_out, ADD_T3_2_out, LDA_T3_2_out, SUB_T3_2_out);
  not not_1 (Cmem, Cmem_out);
  not NOT_Lir (Lir, T2);
  not NOT_Lor (Lor, OUT_T3_out);
  not NOT_Lbr (Lbr, Lbr_out);
  not NOT_Lor_2 (Lar, Lor_out);
  not NOT_Lmar (Lmar, Lmar_out);
  not not_2 (Eir, or_1_out);

  assign Cpc = T1;
  assign Epc = T0;

  // Other names for the same wires on the sheet: ADD = AD
endmodule

// Som. Sub.
module Somador_Subtrator (
  input  [7:0] A,
  input  [7:0] B,
  input  Salu,
  input  Ealu,
  output [7:0] Out
);

  wire [7:0] mux2x8_1_out_4, not_1_out, somador_8_bits_1_r;

  MUX2x8 mux2x8_1 (.A(B), .B(not_1_out), .SEL(Salu), .out_4(mux2x8_1_out_4));
  assign not_1_out = ~B;  // NOT_Gate not_1, 8 bits wide
  Somador_8_bits somador_8_bits_1 (.Ci(Salu), .A(A), .B(mux2x8_1_out_4), .R(somador_8_bits_1_r));
  assign Out = Ealu ? somador_8_bits_1_r : 8'bz;  // Controlled_Buffer controlled_buffer_1
endmodule

// Cont de Prog.
module Contador_de_Programa (
  input  Cpc,
  input  CLK,
  input  CLR,
  input  Epc,
  output [7:0] Out
);

  wire and_1_out;
  wire [4:0] COntador_de_5bit_q0;
  wire [7:0] bit_extender_1_out;

  and and_1 (and_1_out, Cpc, CLK);
  Contador_5bit COntador_de_5bit (
    .E(Cpc), .Clk(and_1_out), .Clr(CLR), .Q4(COntador_de_5bit_q0[4]), .Q3(COntador_de_5bit_q0[3]),
    .Q2(COntador_de_5bit_q0[2]), .Q1(COntador_de_5bit_q0[1]), .Q0(COntador_de_5bit_q0[0]));
  assign bit_extender_1_out = {{3{1'b0}}, COntador_de_5bit_q0};  // Bit_Extender bit_extender_1
  assign Out = Epc ? bit_extender_1_out : 8'bz;  // Controlled_Buffer controlled_buffer_1
endmodule

// FF JK
module Flip_Flop_JK (
  input  K,
  input  J,
  input  Clk,
  input  Pre,
  input  Clr,
  output Q
);

  wire and_1_out, and_2_out, ff_rs_1_nq;

  and and_1 (and_1_out, Q, K);
  and and_2 (and_2_out, J, ff_rs_1_nq);
  Flip_Flop_RS ff_rs_1 (.R(and_1_out), .S(and_2_out), .Clk(Clk), .Pre(Pre), .Clr(Clr), .Q(Q), .nQ(ff_rs_1_nq));
endmodule

module Contador_5bit (
  input  E,
  input  Clk,
  input  Clr,
  output Q4,
  output Q3,
  output Q2,
  output Q1,
  output Q0
);

  wire and_1_out, and_2_out, and_3_out;

  Flip_Flop_JK ff_jk_1 (.K(E), .J(E), .Clk(Clk), .Pre(1'b0), .Clr(Clr), .Q(Q0));
  Flip_Flop_JK ff_jk_2 (.K(Q0), .J(Q0), .Clk(Clk), .Pre(1'b0), .Clr(Clr), .Q(Q1));
  and and_1 (and_1_out, Q0, Q1);
  Flip_Flop_JK ff_jk_3 (.K(and_1_out), .J(and_1_out), .Clk(Clk), .Pre(1'b0), .Clr(Clr), .Q(Q2));
  and and_2 (and_2_out, Q0, and_1_out, Q2);
  Flip_Flop_JK ff_jk_4 (.K(and_2_out), .J(and_2_out), .Clk(Clk), .Pre(1'b0), .Clr(Clr), .Q(Q3));
  and and_3 (and_3_out, Q0, and_1_out, and_2_out, Q3);
  Flip_Flop_JK ff_jk_5 (.K(and_3_out), .J(and_3_out), .Clk(Clk), .Pre(1'b0), .Clr(Clr), .Q(Q4));
endmodule
