// Logisim project DECODER.circ as structural Verilog: 1 circuit, main circuit main
module main (
  input  A0,
  input  A1,
  output O0,
  output O1,
  output O2,
  output O3
);

  wire not_1_out, not_2_out;

  not not_1 (not_1_out, A0);
  not not_2 (not_2_out, A1);
  and and_1 (O0, not_1_out, not_2_out);
  and and_2 (O1, A0, not_2_out);
  and and_3 (O2, not_1_out, A1);
  and and_4 (O3, A0, A1);
endmodule
