// Logisim project MUX - 160891 150995.circ as structural Verilog: 1 circuit, main circuit mux2
module mux2 (
  input  [7:0] E0,
  input  [7:0] E1,
  input  [7:0] A0,
  output [7:0] S
);

  wire [7:0] and_1_out, and_2_out, not_1_out;

  assign not_1_out = ~A0;  // NOT_Gate not_1, 8 bits wide
  assign and_1_out = E0 & not_1_out;  // AND_Gate and_1, 8 bits wide
  assign and_2_out = E1 & A0;  // AND_Gate and_2, 8 bits wide
  assign S = and_1_out | and_2_out;  // OR_Gate or_1, 8 bits wide
endmodule
