// Logisim project MUX.circ as structural Verilog
module main (
);

  mux2 mux2 ();  // open: E0, E1, A0, S
endmodule

module mux2 (
  input  E0,
  input  E1,
  input  A0,
  output S
);

  wire and_1_out, and_2_out, not_1_out;

  not not_1 (not_1_out, A0);
  and and_1 (and_1_out, E0, not_1_out);
  and and_2 (and_2_out, E1, A0);
  or or_1 (S, and_1_out, and_2_out);
endmodule
