// Logisim project Soma 160891 150995.circ as structural Verilog: 1 circuit, main circuit main
module main (
  input  [7:0] A2,
  input  [7:0] A3,
  output [7:0] out_3
);

  Adder adder_1 (.a(A2), .b(A3), .out(out_3));  // open: cin, cout
endmodule
